# Fritzing sketch 06 (saved by Fritzing 0.9.7b)

parts:
  R2 = Rotary Potentiometer (Small) [maximum_resistance=100kΩ package=THT]
  R3 = Rotary Potentiometer (Small) [maximum_resistance=100kΩ package=THT]
  R5 = Rotary Potentiometer (Small) [maximum_resistance=100kΩ package=THT]
  R1 = Rotary Potentiometer (Small) [maximum_resistance=100kΩ package=THT]
  R4 = Rotary Potentiometer (Small) [maximum_resistance=10kΩ package=THT]
  R6 = Rotary Potentiometer (Small) [maximum_resistance=100kΩ package=THT]
  R7 = Resistor [tolerance=±5% power=0.25 resistance=4.7k package=THT]
  U1 = 2.5mm Audio Jack [package=stereojack2.5mm_stereojack2.5mm]
  Компонент1 = Arduino Uno (Rev3)

nets:
  N1: R2.wiper, Компонент1.A2
  N2: R3.wiper, Компонент1.A3
  N3: R5.wiper, Компонент1.A5/SCL
  N4: R1.wiper, Компонент1.A1
  N5: R1.leg2, Компонент1.5V
  N6: R4.wiper, Компонент1.A4/SDA
  N7: R6.wiper, U1.RIGHT
  N8: R6.leg2, R7.Pin_0
  N9: R7.Pin_1, Компонент1.A0
  N10: U1.SLEEVE, Компонент1.GND

notes:
  к 4-канальному шлейфу клавиатуры
  к 8-канальному шлейфу клавиатуры
